// Logisim project da1_task3.circ as structural Verilog: 3 circuits, main circuit DUT
module DUT (
  input  X,
  input  CLK,
  input  RST,
  output Z
);

  wire nand_1_out, nand_2_out, nand_3_out, nand_4_out, nand_5_out, nand_6_out, nand_7_out, nand_8_out,
       nand_9_out, nand_10_out, nand_11_out, nand_12_out, nand_13_out, nand_17_out, nand_18_out, nand_19_out,
       nand_20_out, nand_21_out, nand_22_out, nand_23_out, nand_24_out, nand_25_out, not_1_out, not_2_out,
       not_3_out, not_4_out, not_5_out, not_7_out, not_8_out, not_9_out, t_ff_1_qn, t_ff_2_qn, t_ff_3_qn;
  wire [2:0] cur, nand_16_out;

  not not_1 (not_1_out, X);
  not not_2 (not_2_out, RST);
  not not_3 (not_3_out, cur[2]);
  not not_4 (not_4_out, cur[1]);
  not not_5 (not_5_out, cur[0]);
  nand nand_1 (nand_1_out, not_3_out, not_4_out, not_5_out);
  nand nand_2 (nand_2_out, not_1_out, not_3_out, cur[1]);
  nand nand_3 (nand_3_out, cur[1], not_5_out);
  nand nand_4 (nand_4_out, X, cur[2], not_4_out, cur[0]);
  nand nand_5 (nand_5_out, not_1_out, not_3_out, cur[0]);
  nand nand_6 (nand_6_out, not_1_out, not_4_out, cur[0]);
  nand nand_7 (nand_7_out, not_3_out, not_4_out, cur[0]);
  nand nand_8 (nand_8_out, X, cur[2], not_5_out);
  nand nand_9 (nand_9_out, not_1_out, cur[2], not_4_out);
  nand nand_10 (nand_10_out, not_1_out, cur[2], not_5_out);
  nand nand_11 (nand_11_out, X, not_3_out, not_4_out);
  nand nand_12 (nand_12_out, X, not_3_out, not_5_out);
  nand nand_13 (nand_13_out, X, cur[2], cur[1], cur[0]);
  not not_6 (Z, nand_1_out);
  nand nand_14 (nand_16_out[2], nand_2_out, nand_3_out, not_2_out, nand_4_out);
  nand nand_15 (nand_16_out[1], nand_5_out, nand_6_out, not_2_out, nand_7_out, nand_8_out);
  nand nand_16 (nand_16_out[0], nand_9_out, nand_10_out, not_2_out, nand_11_out, nand_12_out, nand_13_out);
  not not_7 (not_7_out, nand_16_out[0]);
  not not_8 (not_8_out, nand_16_out[1]);
  not not_9 (not_9_out, nand_16_out[2]);
  nand nand_17 (nand_17_out, cur[0], not_7_out);
  nand nand_18 (nand_18_out, nand_17_out, nand_19_out);
  nand nand_19 (nand_19_out, t_ff_1_qn, nand_16_out[0]);
  nand nand_20 (nand_20_out, cur[1], not_8_out);
  nand nand_21 (nand_21_out, nand_20_out, nand_22_out);
  nand nand_22 (nand_22_out, t_ff_2_qn, nand_16_out[1]);
  nand nand_23 (nand_23_out, cur[2], not_9_out);
  nand nand_24 (nand_24_out, nand_23_out, nand_25_out);
  nand nand_25 (nand_25_out, t_ff_3_qn, nand_16_out[2]);
  T_Flip_Flop t_ff_1 (.T(nand_18_out), .clk(CLK), .Q(cur[0]), .Qn(t_ff_1_qn));  // open: reset, preset
  T_Flip_Flop t_ff_2 (.T(nand_21_out), .clk(CLK), .Q(cur[1]), .Qn(t_ff_2_qn));  // open: reset, preset
  T_Flip_Flop t_ff_3 (.T(nand_24_out), .clk(CLK), .Q(cur[2]), .Qn(t_ff_3_qn));  // open: reset, preset

  // Other names for the same wires on the sheet: c = CLK

  // Notes on the sheet:
  //   Please put your deisgn below. You may also use subcircuits.
  //   However, do not move, rename, add, or delete any pins.
endmodule

module TB (
);

  wire clk_out, mypor_1_p2, not_1_out, RESET_out, TimeIndex_carry, undriven;
  wire [0:0] dut_1_z;
  wire [4:0] TimeIndex_q;

  Clock #(.highDuration(2), .lowDuration(2)) clk (.out(clk_out));
  Clock sysclk ();  // open: out
  Counter #(.max('h1f), .ongoal("stay"), .width(5)) TimeIndex (
    .load(clk_out), .clk(clk_out), .D({5{1'b0}}), .carry(TimeIndex_carry), .Q(TimeIndex_q));  // open: clr, up, count
  // MyPOR mypor_1: pin names not known; wires that end beside it: clk_out, mypor_1_p2
  Button RESET (.out(RESET_out));
  ROM #(.addrWidth(5), .dataWidth(1)) TestTraceMemory (.addr(TimeIndex_q));  // open: data
  or or_1 (clk_out, mypor_1_p2, RESET_out);
  not not_1 (not_1_out, TimeIndex_carry);
  DUT dut_1 (.X(undriven), .CLK(clk_out), .RST(clk_out), .Z(dut_1_z[0]));
  TTY tty_1 (.data({6'b011000, dut_1_z[0]}), .clk(clk_out), .we(not_1_out), .clr(clk_out));
  LED DONE (.in(TimeIndex_carry));

  // Notes on the sheet:
  //   DO NOT MODIFY THIS
  //   YOU MAY TEST YOUR CIRCUITS USING THIS TO MAKE SURE YOU HAVE NOT ALTERED PIN OUT
  //   Edit ROM with input trace of 32 bits
endmodule

module TBRANDOM (
);

  wire clk_out, mypor_1_p2, not_1_out, random_1_out, RESET_out, TimeIndex_carry;
  wire [0:0] dut_1_z;

  Clock #(.highDuration(2), .lowDuration(2)) clk (.out(clk_out));
  Clock sysclk ();  // open: out
  Counter #(.ongoal("stay")) TimeIndex (
    .load(clk_out), .clk(clk_out), .D({8{1'b0}}), .carry(TimeIndex_carry));  // open: clr, up, count, Q
  // MyPOR mypor_1: pin names not known; wires that end beside it: clk_out, mypor_1_p2
  Button RESET (.out(RESET_out));
  or or_1 (clk_out, mypor_1_p2, RESET_out);
  Random #(.width(1)) random_1 (.clr(clk_out), .clk(clk_out), .out(random_1_out));  // open: next
  not not_1 (not_1_out, TimeIndex_carry);
  DUT dut_1 (.X(random_1_out), .CLK(clk_out), .RST(clk_out), .Z(dut_1_z[0]));
  TTY tty_1 (.data({6'b011000, dut_1_z[0]}), .clk(clk_out), .we(not_1_out), .clr(clk_out));
  LED DONE (.in(TimeIndex_carry));

  // Notes on the sheet:
  //   DO NOT MODIFY THIS
  //   YOU MAY TEST YOUR CIRCUITS USING THIS TO MAKE SURE YOU HAVE NOT ALTERED PIN OUT
endmodule
