// Logisim project da1_task4.circ as structural Verilog: 2 circuits, main circuit DUT
module DUT (
  input  [15:0] DIN1,
  input  [15:0] DIN2,
  input  [15:0] DIN3,
  input  GO1,
  input  GO2,
  input  GO3,
  input  CLK,
  input  RST,
  output [15:0] DOUT,
  output DONE
);


  // Notes on the sheet:
  //   Please put your design below. You may also use subcircuits.
  //   However, do not move, rename, add, or delete any pins.
endmodule

module TB (
  input  [15:0] DIN1,
  input  [15:0] DIN2,
  input  [15:0] DIN3,
  input  GO1,
  input  GO2,
  input  GO3,
  input  RST,
  output [15:0] DOUT,
  output DONE
);

  wire clk_out, or_1_out, RESET_out;

  Clock sysclk ();  // open: out
  Button RESET (.out(RESET_out));
  Clock #(.highDuration(2), .lowDuration(2)) clk (.out(clk_out));
  or or_1 (or_1_out, RESET_out, RST);
  DUT dut_1 (
    .DIN1(DIN1), .DIN2(DIN2), .DIN3(DIN3), .GO1(GO1), .GO2(GO2), .GO3(GO3), .CLK(clk_out), .RST(or_1_out),
    .DOUT(DOUT), .DONE(DONE));

  // Notes on the sheet:
  //   DO NOT MODIFY THIS
  //   YOU MAY TEST YOUR CIRCUITS USING THIS TO MAKE SURE YOU HAVE NOT ALTERED PIN OUT
endmodule
